// Logisim project Final_project.circ as structural Verilog: 6 circuits, main circuit TRAFFIC_LIGHT_1
module TRAFFIC_LIGHT_1 (
  output RED,
  output YELLOW,
  output GREEN
);

  wire clock_2_out, not_1_out;

  Clock #(.highDuration(6), .lowDuration(8)) clock_1 (.out(GREEN));
  not not_1 (not_1_out, GREEN);
  Clock #(.highDuration(8), .lowDuration(6)) clock_2 (.out(clock_2_out));
  nor nor_1 (RED, GREEN, YELLOW);
  and and_1 (YELLOW, clock_2_out, not_1_out);

  // Notes on the sheet:
  //   Cycle = 7 sec
  //   Green 3 sec
  //   red 3 sec
  //   yellow 1 sec
endmodule

module vol_1 (
);

  wire traffic_light_1_1_green, traffic_light_1_1_red, traffic_light_1_1_yellow;

  TRAFFIC_LIGHT_1 traffic_light_1_1 (
    .RED(traffic_light_1_1_red), .YELLOW(traffic_light_1_1_yellow), .GREEN(traffic_light_1_1_green));
  LED led_1 (.in(traffic_light_1_1_red));
  LED led_2 (.in(traffic_light_1_1_yellow));
  LED led_3 (.in(traffic_light_1_1_green));
endmodule

module TRAFFIC_LIGHT_2 (
  output out_1,
  output out_2,
  output out_3
);

  wire clock_1_out, d_ff_1_qn, d_ff_2_q;

  Clock clock_1 (.out(clock_1_out));
  D_Flip_Flop d_ff_1 (.clk(clock_1_out), .D(d_ff_1_qn), .Qn(d_ff_1_qn));  // open: Q, preset, en, reset
  D_Flip_Flop d_ff_2 (.clk(d_ff_1_qn), .D(out_3), .Q(d_ff_2_q), .Qn(out_3));  // open: preset, en, reset
  and and_1 (out_1, d_ff_1_qn, d_ff_2_q);
  nor nor_1 (out_2, out_1, out_3);
endmodule

module vol_2 (
);

  wire traffic_light_2_1_out_1, traffic_light_2_1_out_2, traffic_light_2_1_out_3;

  TRAFFIC_LIGHT_2 traffic_light_2_1 (
    .out_1(traffic_light_2_1_out_1), .out_2(traffic_light_2_1_out_2), .out_3(traffic_light_2_1_out_3));
  LED led_1 (.in(traffic_light_2_1_out_1));
  LED led_2 (.in(traffic_light_2_1_out_2));
  LED led_3 (.in(traffic_light_2_1_out_3));
endmodule

module vol_3 (
);

  wire and_1_out, and_2_out, and_3_out, clock_1_out, clock_2_out, clock_3_out, counter_1_carry,
       counter_3_carry, d_ff_1_q, d_ff_2_q, enable_1_out_1, enable_1_out_2, enable_1_out_3;
  wire [3:0] counter_1_q, counter_2_q, counter_3_q, counter_4_q, counter_5_q, counter_6_q;

  Enable enable_1 (.out_1(enable_1_out_1), .out_2(enable_1_out_2), .out_3(enable_1_out_3));
  Clock clock_1 (.out(clock_1_out));
  Clock clock_2 (.out(clock_2_out));
  Clock clock_3 (.out(clock_3_out));
  Counter #(.width(4), .max('h9)) counter_1 (
    .load(1'b1), .Q(counter_1_q), .carry(counter_1_carry), .clk(and_1_out), .clr(enable_1_out_2));  // open: D, count
  and and_1 (and_1_out, enable_1_out_1, clock_1_out);
  Counter #(.width(4), .max('h9)) counter_2 (
    .load(1'b1), .Q(counter_2_q), .clk(and_2_out));  // open: D, count, carry, clr
  and and_2 (and_2_out, enable_1_out_2, clock_2_out);
  Counter #(.width(4), .max('h9)) counter_3 (
    .load(1'b1), .Q(counter_3_q), .carry(counter_3_carry), .clk(and_3_out), .clr(enable_1_out_2));  // open: D, count
  and and_3 (and_3_out, enable_1_out_3, clock_3_out);
  D_Flip_Flop d_ff_1 (.clk(and_3_out), .D(counter_3_carry), .Q(d_ff_1_q));  // open: Qn, preset, en, reset
  Counter #(.width(4), .max('h2)) counter_4 (
    .load(1'b1), .Q(counter_4_q), .clk(d_ff_2_q), .clr(enable_1_out_2));  // open: D, count, carry
  D_Flip_Flop d_ff_2 (.clk(and_1_out), .D(counter_1_carry), .Q(d_ff_2_q));  // open: Qn, preset, en, reset
  Counter #(.width(4), .max('hf)) counter_5 (.Q(counter_5_q));  // open: load, D, count, carry, clk, clr
  Hex_Digit_Display hex_digit_display_1 (.value(counter_5_q));  // open: dp
  Counter #(.width(4), .max('h2)) counter_6 (
    .load(1'b1), .Q(counter_6_q), .clk(d_ff_1_q), .clr(enable_1_out_2));  // open: D, count, carry
  Hex_Digit_Display hex_digit_display_2 (.value(counter_2_q));  // open: dp
  Hex_Digit_Display hex_digit_display_3 (.value(counter_4_q));  // open: dp
  Hex_Digit_Display hex_digit_display_4 (.value(counter_6_q));  // open: dp
  Hex_Digit_Display hex_digit_display_5 (.value(counter_1_q));  // open: dp
  Hex_Digit_Display hex_digit_display_6 (.value(counter_3_q));  // open: dp
endmodule

module Enable (
  output out_1,
  output out_2,
  output out_3
);

  wire and_1_out, clock_1_out;
  wire [1:0] counter_1_q;

  Counter #(.width(3), .max('h6)) counter_1 (
    .Q({out_3, counter_1_q}), .clk(clock_1_out));  // open: load, D, count, carry, clr
  Clock #(.highDuration(10), .lowDuration(10)) clock_1 (.out(clock_1_out));
  and and_1 (and_1_out, counter_1_q[1], counter_1_q[0]);
  nor nor_1 (out_1, out_3, and_1_out);
  and and_2 (out_2, counter_1_q[1], counter_1_q[0]);
endmodule
